# Fritzing sketch Circuit_Diagram (saved by Fritzing 0.9.3b)
breadboards: 1

parts:
  Part1 = TFT 2.2 inch 320x240 w microSD [part_number=1480]
  Part2 = Adafruit Feather 328P [part_number="Adafruit #3458"]
  S3 = Pushbutton [package="[THT]"]
  S2 = Pushbutton [package="[THT]"]
  S1 = Pushbutton [package="[THT]"]
  S4 = Pushbutton [package="[THT]"]

nets:
  GND: Part1.GND, Part2.GND, S2.Pin_1, S2.Pin_2, S1.Pin_1, S1.Pin_2, S4.Pin_1, S4.Pin_2
  VIN: Part1.VIN, Part2.3.3V
  N1: Part1.DC, Part2.D9
  N2: Part1.RESET, Part2.RESET
  N3: Part1.SDCS, Part2.D5
  N4: Part1.LCDCS, Part2.D6
  N5: Part1.MOSI, Part2.D11/MOSI
  N6: Part1.MISO, Part2.D12/MISO
  N7: Part1.SCLK, Part2.D13/SCK
  N8: Part1.BACKLIGHT, Part2.D10
  N9: Part2.A3, S1.Pin_3, S1.Pin_4
  N10: Part2.D4, S4.Pin_3, S4.Pin_4
  N11: Part2.D3, S3.Pin_3, S3.Pin_4
  N12: Part2.D2, S2.Pin_3, S2.Pin_4
  N13: S3.Pin_1, S3.Pin_2

custom parts:
  TFT 2.2 inch 320x240 w microSD: This lovely little display breakout is the best way to add a small, colorful and bright display to any project. Since the display uses 4-wire SPI to communicate and has its own pixel-addressable frame buffer, it can be used with every kind of microcontroller. Even a very small one with low memory and few pins available! The 2.2" display has 320x240 color pixels.
  Adafruit Feather 328P: With this Feather we're getting a little nostalgic for the ATmega328P - the classic 'Arduino' chip - with this Adafruit Feather 328P running a 3.3V and 8 MHz. Feather is the new development board from Adafruit, and like it's namesake it is thin, light, and lets you fly! We designed Feather to be a new standard for portable microcontroller cores. We have other boards in the Feather family,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
